# Fritzing sketch pico-macro-key (saved by Fritzing 0.9.8b)
circuit board: 8.46667cm x 5.64444cm
breadboards: 1

parts:
  Raspberry_Pi_Pico = Raspberry Pi Pico
  Button1 = Round Pushbutton
  Button2 = Round Pushbutton
  Shift_Button = Square Pushbutton
  Button3 = Round Pushbutton
  Buzzer = Buzzer 12mm [package=buzzer-12mm]
  LCD_Mono_128x32 = 128x32 I2C Monochrome OLED Display

nets:
  N1: Raspberry_Pi_Pico.pin_3, Raspberry_Pi_Pico.pin_8, Raspberry_Pi_Pico.pin_13, Raspberry_Pi_Pico.pin_18, Raspberry_Pi_Pico.pin_23, Raspberry_Pi_Pico.pin_28, Raspberry_Pi_Pico.pin_33, Raspberry_Pi_Pico.pin_38, Buzzer.1, LCD_Mono_128x32.GND
  N2: Raspberry_Pi_Pico.pin_6, Button3.leg1
  N3: Raspberry_Pi_Pico.pin_10, Button2.leg1
  N4: Raspberry_Pi_Pico.pin_14, Button1.leg1
  N5: Raspberry_Pi_Pico.pin_17, Shift_Button.leg1
  N6: Raspberry_Pi_Pico.pin_21, Buzzer.2
  N7: Raspberry_Pi_Pico.pin_26, LCD_Mono_128x32.SDA
  N8: Raspberry_Pi_Pico.pin_27, LCD_Mono_128x32.SCL
  N9: Raspberry_Pi_Pico.pin_37, Button1.leg0, Button2.leg0, Shift_Button.leg0, Button3.leg0, LCD_Mono_128x32.3.3V

custom parts:
  Raspberry Pi Pico: Raspberry Pi Pico. Based around the RP2040 microcontroller the Pico is a low cost microcontroller device bringing Raspberry Pi quality, cost, and easy of use to the microcontroller space. Jan 2021, Split part in to two versions: tht (this one) and SMD. This one will drill holes for a .1 in header in pcb to allow plugging in the module as well as providing pads to solder the module to the top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
